# Fritzing sketch connections (saved by Fritzing 0.9.2b)
breadboards: 1

parts:
  Composant1 = Arduino Micro (Rev3)
  BAT1 = Battery Holders [package=lipo-1100mAh]
  U1 = 556 [package=dil14]
  S1 = Momentary Switch [package=ksa_sealed_tac_switch]
  S2 = Momentary Switch [package=ksa_sealed_tac_switch]

nets:
  N1: Composant1.D4_PWM/A6, U1.THR
  VIN: Composant1.VIN, BAT1.+, U1.VCC, S1.1, S2.1
  GND: Composant1.GND, BAT1.-, U1.DIS, U1.GND, S1.4, S2.4
  N2: U1.CV, S1.3
  N3: S1.2, S2.3

notes:
  74AHCT125
  NeoPixels
